// Logisim project 8 Bit Adder.circ as structural Verilog: 1 circuit, main circuit main
module main (
  input  [7:0] A,
  input  in_2,
  input  [7:0] B,
  output out_4
);

  wire main_1_c_out;
  wire [3:0] main_1_s_out;
  wire [7:4] main_2_s_out;

  _4_Bit_Adder_main main_1 (.S_out(main_1_s_out), .A(A[3:0]), .C_in(in_2), .B(B[3:0]), .C_out(main_1_c_out));
  // Probe on {main_2_s_out, main_1_s_out}
  _4_Bit_Adder_main main_2 (.S_out(main_2_s_out), .A(A[7:4]), .C_in(main_1_c_out), .B(B[7:4]), .C_out(out_4));
endmodule
